# Fritzing sketch Schema (saved by Fritzing 0.9.2b)
breadboards: 1

parts:
  Raspberry_Pi1 = Raspberry Pi B+
  LED1 = RGB LED (com. cathode, rbg) [package="5 mm [THT]"]
  R1 = Resistor [tolerance=±20% resistance=470 package="2512 [SMD]"]
  R2 = Resistor [tolerance=±20% resistance=470 package="2512 [SMD]"]
  R3 = Resistor [tolerance=±20% resistance=470 package="2512 [SMD]"]

nets:
  N1: Raspberry_Pi1.GPIO21, R3.Pin_0
  N2: Raspberry_Pi1.GPIO20, R2.Pin_0
  N3: Raspberry_Pi1.GPIO16, R1.Pin_0
  N4: Raspberry_Pi1.GND, LED1.common_cathode
  N5: LED1.red_anode, R1.Pin_1
  N6: LED1.blue_anode, R2.Pin_1
  N7: LED1.green_anode, R3.Pin_1

notes:
  R : GPIO 16 (pin 36)
  B : GPIO 20 (pin 38)
  G : GPIO 21 (pin 40)
